// Digital circuit 165-mem.dig as structural Verilog
module _165_mem (
  input  D,
  input  SER,
  input  SH_nLD,
  input  C,
  output Q
);

  wire and_1_out, and_2_out;

  and and_1 (and_1_out, D, ~SH_nLD);  // And
  and and_2 (and_2_out, ~and_1_out, ~SH_nLD);  // And
  D_FF_AS d_ff_as_1 (.Set(and_1_out), .D(SER), .C(C), .Clr(and_2_out), .Q(Q));  // open: nQ

  // Notes on the sheet:
  //   D' is an asynchronous D
  //   shift/load input
endmodule
