// Digital circuit p2s-74HC165.dig as structural Verilog
module p2s_74HC165 (
  input  SER,
  input  CLK,
  input  CLK_INH,
  input  SH_nLD,
  input  A,
  input  B,
  input  C,
  input  D,
  input  E,
  input  F,
  input  G,
  input  H,
  output nQH,
  output QH
);

  wire _165_mem_1_q, _165_mem_2_q, _165_mem_3_q, _165_mem_4_q, _165_mem_5_q, _165_mem_6_q, _165_mem_7_q,
       or_1_out;

  or or_1 (or_1_out, CLK, CLK_INH);
  _165_mem _165_mem_1 (.D(A), .SER(SER), .SH_nLD(SH_nLD), .C(or_1_out), .Q(_165_mem_1_q));
  _165_mem _165_mem_2 (.D(B), .SER(_165_mem_1_q), .SH_nLD(SH_nLD), .C(or_1_out), .Q(_165_mem_2_q));
  _165_mem _165_mem_3 (.D(C), .SER(_165_mem_2_q), .SH_nLD(SH_nLD), .C(or_1_out), .Q(_165_mem_3_q));
  _165_mem _165_mem_4 (.D(D), .SER(_165_mem_3_q), .SH_nLD(SH_nLD), .C(or_1_out), .Q(_165_mem_4_q));
  _165_mem _165_mem_5 (.D(E), .SER(_165_mem_4_q), .SH_nLD(SH_nLD), .C(or_1_out), .Q(_165_mem_5_q));
  _165_mem _165_mem_6 (.D(F), .SER(_165_mem_5_q), .SH_nLD(SH_nLD), .C(or_1_out), .Q(_165_mem_6_q));
  _165_mem _165_mem_7 (.D(G), .SER(_165_mem_6_q), .SH_nLD(SH_nLD), .C(or_1_out), .Q(_165_mem_7_q));
  _165_mem _165_mem_8 (.D(H), .SER(_165_mem_7_q), .SH_nLD(SH_nLD), .C(or_1_out), .Q(QH));
  not not_1 (nQH, QH);

  // Notes on the sheet:
  //   SH_nLD: default 1
  //   A: default 1
  //   B: default 1
  //   D: default 1
  //   F: default 1
  //   H: default 1
  //   shift/load input
endmodule

/* Test case:
# ---------- 74HC165 ----------
# Paste into a Test component in p2s-74HC165.dig.
SH/~LD CLK CLK_INH SER A B C D E F G H QH ~QH
# parallel load A..H = 1,1,0,1,0,0,1,0: QH shows H straight away
0 0 0 0 1 1 0 1 0 0 1 0 0 1
# load released: changing the inputs now has no effect
1 0 0 0 0 0 1 1 1 0 0 1 0 1
# seven clocks: QH shows G, F, E, D, C, B, A in turn
1 1 0 0 0 0 1 1 1 0 0 1 1 0
1 0 0 0 0 0 1 1 1 0 0 1 1 0
1 1 0 0 0 0 1 1 1 0 0 1 0 1
1 0 0 0 0 0 1 1 1 0 0 1 0 1
1 1 0 0 0 0 1 1 1 0 0 1 0 1
1 0 0 0 0 0 1 1 1 0 0 1 0 1
1 1 0 0 0 0 1 1 1 0 0 1 1 0
1 0 0 0 0 0 1 1 1 0 0 1 1 0
1 1 0 0 0 0 1 1 1 0 0 1 0 1
1 0 0 0 0 0 1 1 1 0 0 1 0 1
1 1 0 0 0 0 1 1 1 0 0 1 1 0
1 0 0 0 0 0 1 1 1 0 0 1 1 0
1 1 0 0 0 0 1 1 1 0 0 1 1 0
1 0 0 0 0 0 1 1 1 0 0 1 1 0
# reload, then shift 1s in through SER
0 0 0 0 1 1 0 1 0 0 1 0 0 1
1 0 0 1 1 1 0 1 0 0 1 0 0 1
1 1 0 1 1 1 0 1 0 0 1 0 1 0
1 0 0 1 1 1 0 1 0 0 1 0 1 0
1 1 0 1 1 1 0 1 0 0 1 0 0 1
1 0 0 1 1 1 0 1 0 0 1 0 0 1
1 1 0 1 1 1 0 1 0 0 1 0 0 1
1 0 0 1 1 1 0 1 0 0 1 0 0 1
1 1 0 1 1 1 0 1 0 0 1 0 1 0
1 0 0 1 1 1 0 1 0 0 1 0 1 0
1 1 0 1 1 1 0 1 0 0 1 0 0 1
1 0 0 1 1 1 0 1 0 0 1 0 0 1
1 1 0 1 1 1 0 1 0 0 1 0 1 0
1 0 0 1 1 1 0 1 0 0 1 0 1 0
1 1 0 1 1 1 0 1 0 0 1 0 1 0
1 0 0 1 1 1 0 1 0 0 1 0 1 0
1 1 0 1 1 1 0 1 0 0 1 0 1 0
1 0 0 1 1 1 0 1 0 0 1 0 1 0
# reload: QH = H = 0. H, G, F alternate, so a missing or extra shift shows on QH
0 0 0 0 1 1 0 1 0 0 1 0 0 1
1 0 0 0 1 1 0 1 0 0 1 0 0 1
# one clock: QH = G = 1
1 1 0 0 1 1 0 1 0 0 1 0 1 0
# raise CLK_INH while CLK is high, then pulse CLK twice: no shift, QH stays 1
1 1 1 0 1 1 0 1 0 0 1 0 1 0
1 0 1 0 1 1 0 1 0 0 1 0 1 0
1 1 1 0 1 1 0 1 0 0 1 0 1 0
1 0 1 0 1 1 0 1 0 0 1 0 1 0
# release CLK_INH while CLK is high, then CLK low: no shift
1 1 1 0 1 1 0 1 0 0 1 0 1 0
1 1 0 0 1 1 0 1 0 0 1 0 1 0
1 0 0 0 1 1 0 1 0 0 1 0 1 0
# one normal clock: QH = F = 0
1 1 0 0 1 1 0 1 0 0 1 0 0 1
1 0 0 0 1 1 0 1 0 0 1 0 0 1
# hazard: raising CLK_INH while CLK is low clocks too. Two rises: QH = E = 0, then D = 1
1 0 1 0 1 1 0 1 0 0 1 0 0 1
1 0 0 0 1 1 0 1 0 0 1 0 0 1
1 0 1 0 1 1 0 1 0 0 1 0 1 0
*/
