// Digital circuit s2p-74HC595-animation.dig as structural Verilog
module s2p_74HC595_animation (
  input  clk,
  output QA,
  output QB,
  output QC,
  output QD,
  output QE,
  output QF,
  output QG,
  output QH,
  output QH_2
);

  wire button_1_out, d_ff_1_q, d_ff_2_q, d_ff_3_q, d_ff_4_q, d_ff_5_q, d_ff_6_q, d_ff_7_q, d_ff_8_q, nOE,
       nSRCLR, RCLK, SER, shift_A_q, shift_B_q, shift_C_q, shift_D_q, shift_E_q, shift_F_q, shift_G_q, SRCLK;
  wire [4:0] counter_1_out;

  Button button_1 (.out(button_1_out));
  Counter #(.Bits(5)) counter_1 (.en(1'b1), .C(clk), .clr(button_1_out), .out(counter_1_out));  // open: ovf
  ROM #(.AddrBits(5), .Bits(5)) rom_1 (.A(counter_1_out), .sel(1'b1), .D({SRCLK, nSRCLR, SER, RCLK, nOE}));
  D_FF_AS shift_A (.Set(1'b0), .D(SER), .C(SRCLK), .Clr(~nSRCLR), .Q(shift_A_q));  // open: nQ
  D_FF d_ff_1 (.D(shift_A_q), .C(RCLK), .Q(d_ff_1_q));  // open: nQ
  D_FF_AS shift_B (.Set(1'b0), .D(shift_A_q), .C(SRCLK), .Clr(~nSRCLR), .Q(shift_B_q));  // open: nQ
  assign QA = ~nOE ? d_ff_1_q : 1'bz;  // DriverInvSel driverinvsel_1
  D_FF d_ff_2 (.D(shift_B_q), .C(RCLK), .Q(d_ff_2_q));  // open: nQ
  D_FF_AS shift_C (.Set(1'b0), .D(shift_B_q), .C(SRCLK), .Clr(~nSRCLR), .Q(shift_C_q));  // open: nQ
  assign QB = ~nOE ? d_ff_2_q : 1'bz;  // DriverInvSel driverinvsel_2
  D_FF d_ff_3 (.D(shift_C_q), .C(RCLK), .Q(d_ff_3_q));  // open: nQ
  D_FF_AS shift_D (.Set(1'b0), .D(shift_C_q), .C(SRCLK), .Clr(~nSRCLR), .Q(shift_D_q));  // open: nQ
  assign QC = ~nOE ? d_ff_3_q : 1'bz;  // DriverInvSel driverinvsel_3
  D_FF d_ff_4 (.D(shift_D_q), .C(RCLK), .Q(d_ff_4_q));  // open: nQ
  D_FF_AS shift_E (.Set(1'b0), .D(shift_D_q), .C(SRCLK), .Clr(~nSRCLR), .Q(shift_E_q));  // open: nQ
  assign QD = ~nOE ? d_ff_4_q : 1'bz;  // DriverInvSel driverinvsel_4
  D_FF d_ff_5 (.D(shift_E_q), .C(RCLK), .Q(d_ff_5_q));  // open: nQ
  D_FF_AS shift_F (.Set(1'b0), .D(shift_E_q), .C(SRCLK), .Clr(~nSRCLR), .Q(shift_F_q));  // open: nQ
  assign QE = ~nOE ? d_ff_5_q : 1'bz;  // DriverInvSel driverinvsel_5
  D_FF d_ff_6 (.D(shift_F_q), .C(RCLK), .Q(d_ff_6_q));  // open: nQ
  D_FF_AS shift_G (.Set(1'b0), .D(shift_F_q), .C(SRCLK), .Clr(~nSRCLR), .Q(shift_G_q));  // open: nQ
  assign QF = ~nOE ? d_ff_6_q : 1'bz;  // DriverInvSel driverinvsel_6
  D_FF d_ff_7 (.D(shift_G_q), .C(RCLK), .Q(d_ff_7_q));  // open: nQ
  D_FF_AS shift_H (.Set(1'b0), .D(shift_G_q), .C(SRCLK), .Clr(~nSRCLR), .Q(QH_2));  // open: nQ
  assign QG = ~nOE ? d_ff_7_q : 1'bz;  // DriverInvSel driverinvsel_7
  D_FF d_ff_8 (.D(QH_2), .C(RCLK), .Q(d_ff_8_q));  // open: nQ
  assign QH = ~nOE ? d_ff_8_q : 1'bz;  // DriverInvSel driverinvsel_8

  // Notes on the sheet:
  //   contents of rom_1 (hex, n*v repeats v):
  //   0,2,8,c,1c,8,18,c,1c,c,1c,8,18,8,18,8,18,c,1c,8,a,8,9,8,0,8,a
  //   ,5*8
  //   serial to parallel
  //   74HC595
endmodule
