// Digital circuit s2p-74HC595.dig as structural Verilog
module s2p_74HC595 (
  input  nOE,
  input  RCLK,
  input  SER,
  input  nSRCLR,
  input  SRCLK,
  output QA,
  output QB,
  output QC,
  output QD,
  output QE,
  output QF,
  output QG,
  output QH,
  output QH_2
);

  wire d_ff_1_q, d_ff_2_q, d_ff_3_q, d_ff_4_q, d_ff_5_q, d_ff_6_q, d_ff_7_q, d_ff_8_q, shift_A_q, shift_B_q,
       shift_C_q, shift_D_q, shift_E_q, shift_F_q, shift_G_q;

  D_FF_AS shift_A (.Set(1'b0), .D(SER), .C(SRCLK), .Clr(~nSRCLR), .Q(shift_A_q));  // open: nQ
  D_FF d_ff_1 (.D(shift_A_q), .C(RCLK), .Q(d_ff_1_q));  // open: nQ
  D_FF_AS shift_B (.Set(1'b0), .D(shift_A_q), .C(SRCLK), .Clr(~nSRCLR), .Q(shift_B_q));  // open: nQ
  assign QA = ~nOE ? d_ff_1_q : 1'bz;  // DriverInvSel driverinvsel_1
  D_FF d_ff_2 (.D(shift_B_q), .C(RCLK), .Q(d_ff_2_q));  // open: nQ
  D_FF_AS shift_C (.Set(1'b0), .D(shift_B_q), .C(SRCLK), .Clr(~nSRCLR), .Q(shift_C_q));  // open: nQ
  assign QB = ~nOE ? d_ff_2_q : 1'bz;  // DriverInvSel driverinvsel_2
  D_FF d_ff_3 (.D(shift_C_q), .C(RCLK), .Q(d_ff_3_q));  // open: nQ
  D_FF_AS shift_D (.Set(1'b0), .D(shift_C_q), .C(SRCLK), .Clr(~nSRCLR), .Q(shift_D_q));  // open: nQ
  assign QC = ~nOE ? d_ff_3_q : 1'bz;  // DriverInvSel driverinvsel_3
  D_FF d_ff_4 (.D(shift_D_q), .C(RCLK), .Q(d_ff_4_q));  // open: nQ
  D_FF_AS shift_E (.Set(1'b0), .D(shift_D_q), .C(SRCLK), .Clr(~nSRCLR), .Q(shift_E_q));  // open: nQ
  assign QD = ~nOE ? d_ff_4_q : 1'bz;  // DriverInvSel driverinvsel_4
  D_FF d_ff_5 (.D(shift_E_q), .C(RCLK), .Q(d_ff_5_q));  // open: nQ
  D_FF_AS shift_F (.Set(1'b0), .D(shift_E_q), .C(SRCLK), .Clr(~nSRCLR), .Q(shift_F_q));  // open: nQ
  assign QE = ~nOE ? d_ff_5_q : 1'bz;  // DriverInvSel driverinvsel_5
  D_FF d_ff_6 (.D(shift_F_q), .C(RCLK), .Q(d_ff_6_q));  // open: nQ
  D_FF_AS shift_G (.Set(1'b0), .D(shift_F_q), .C(SRCLK), .Clr(~nSRCLR), .Q(shift_G_q));  // open: nQ
  assign QF = ~nOE ? d_ff_6_q : 1'bz;  // DriverInvSel driverinvsel_6
  D_FF d_ff_7 (.D(shift_G_q), .C(RCLK), .Q(d_ff_7_q));  // open: nQ
  D_FF_AS shift_H (.Set(1'b0), .D(shift_G_q), .C(SRCLK), .Clr(~nSRCLR), .Q(QH_2));  // open: nQ
  assign QG = ~nOE ? d_ff_7_q : 1'bz;  // DriverInvSel driverinvsel_7
  D_FF d_ff_8 (.D(QH_2), .C(RCLK), .Q(d_ff_8_q));  // open: nQ
  assign QH = ~nOE ? d_ff_8_q : 1'bz;  // DriverInvSel driverinvsel_8

  // Notes on the sheet:
  //   nSRCLR: default 1
endmodule

/* Test case:
~SRCLR SER SRCLK RCLK ~OE QA QB QC QD QE QF QG QH QH'
# clear the shift register (storage still unknown)
0 0 0 0 0 X X X X X X X X 0
# RCLK edge: copy the cleared register to the outputs
0 0 0 1 0 0 0 0 0 0 0 0 0 0
1 0 0 0 0 0 0 0 0 0 0 0 0 0
# shift in 1,0,1,1,0,0,0,1; outputs must not change yet
1 1 0 0 0 0 0 0 0 0 0 0 0 0
1 1 1 0 0 0 0 0 0 0 0 0 0 0
1 0 0 0 0 0 0 0 0 0 0 0 0 0
1 0 1 0 0 0 0 0 0 0 0 0 0 0
1 1 0 0 0 0 0 0 0 0 0 0 0 0
1 1 1 0 0 0 0 0 0 0 0 0 0 0
1 1 0 0 0 0 0 0 0 0 0 0 0 0
1 1 1 0 0 0 0 0 0 0 0 0 0 0
1 0 0 0 0 0 0 0 0 0 0 0 0 0
1 0 1 0 0 0 0 0 0 0 0 0 0 0
1 0 0 0 0 0 0 0 0 0 0 0 0 0
1 0 1 0 0 0 0 0 0 0 0 0 0 0
1 0 0 0 0 0 0 0 0 0 0 0 0 0
1 0 1 0 0 0 0 0 0 0 0 0 0 0
1 1 0 0 0 0 0 0 0 0 0 0 0 0
1 1 1 0 0 0 0 0 0 0 0 0 0 1
1 0 0 0 0 0 0 0 0 0 0 0 0 1
# RCLK edge: pattern appears at once (QA = last bit in, QH = first)
1 0 0 1 0 1 0 0 0 1 1 0 1 1
1 0 0 0 0 1 0 0 0 1 1 0 1 1
# ~OE high: outputs float, QH' still driven
1 0 0 0 1 Z Z Z Z Z Z Z Z 1
# ~OE low again
1 0 0 0 0 1 0 0 0 1 1 0 1 1
# clear: QHp drops at once, outputs keep the old pattern
0 0 0 0 0 1 0 0 0 1 1 0 1 0
1 0 0 0 0 1 0 0 0 1 1 0 1 0
# RCLK edge: the cleared register reaches the outputs
1 0 0 1 0 0 0 0 0 0 0 0 0 0
1 0 0 0 0 0 0 0 0 0 0 0 0 0
*/
